// Logisim project CIRCUIT.circ as structural Verilog: 1 circuit, main circuit main
module main (
  input  ENABLE,
  input  DAY_NIGHT,
  input  MOBILITY,
  output FULL_BRIGHTNESS,
  output DIM_BRIGHTNESS
);

  wire not_1_out;

  not not_1 (not_1_out, MOBILITY);
  and FULL (FULL_BRIGHTNESS, ENABLE, DAY_NIGHT, MOBILITY);
  and DIM (DIM_BRIGHTNESS, not_1_out, DAY_NIGHT, ENABLE);
endmodule
